// Logisim project ALU.circ as structural Verilog: 9 circuits, main circuit Main
// ALU8
module Main (
  input  [7:0] A,
  input  [7:0] B,
  input  Cin,
  input  [3:0] Selector_PIn,
  output ZF,
  output SF,
  output [7:0] _8_bits_output,
  output OF,
  output Cout
);

  wire add8_1_cout, Addl_cout, left_shift_1_cout, not_2_out, right_shift_1_cout;
  wire [7:0] add8_1_out_4, Addl_out_4, and_1_out, left_shift_1_out_3, not_1_out, right_shift_1_out_4,
       xor_1_out;

  assign not_1_out = ~A;  // NOT_Gate not_1, 8 bits wide
  Left_Shift left_shift_1 (.Cin(Cin), .Input(A), .Cout(left_shift_1_cout), .out_3(left_shift_1_out_3));
  assign and_1_out = A & B;  // AND_Gate and_1, 8 bits wide
  add8 Addl (.First_8_bits_input(not_1_out), .Second_8_bits_input(B), .Cin(Cin), .Cout(Addl_cout), .out_4(Addl_out_4));
  assign xor_1_out = A ^ B;  // XOR_Gate xor_1, 8 bits wide
  add8 add8_1 (.First_8_bits_input(A), .Second_8_bits_input(B), .Cin(Cin), .Cout(add8_1_cout), .out_4(add8_1_out_4));
  Right_Shift right_shift_1 (.in_1(A), .Cin(Cin), .Cout(right_shift_1_cout), .out_4(right_shift_1_out_4));
  ZF u_ZF (.in_1(_8_bits_output), .out_2(ZF));
  Multiplexer #(.select(4), .width(8)) multiplexer_1 (
    .in0(add8_1_out_4), .in1(Addl_out_4), .in2(and_1_out), .in3(xor_1_out), .in4(right_shift_1_out_4),
    .in5(left_shift_1_out_3), .out(_8_bits_output), .sel(Selector_PIn));  // open: in6, in7, in8, in9, in10, in11, in12, in13, in14, in15, en
  SF u_SF (.in_1(_8_bits_output), .SF(SF));
  OF of_1 (.Input_A(xor_1_out), .Input_B(and_1_out), .OF(OF), .Selector(Selector_PIn), .Output(_8_bits_output));
  not not_2 (not_2_out, 1'b1);
  Multiplexer #(.select(4)) multiplexer_2 (
    .in0(add8_1_cout), .in1(Addl_cout), .in2(not_2_out), .in3(not_2_out), .in4(right_shift_1_cout),
    .in5(left_shift_1_cout), .out(Cout), .sel(Selector_PIn));  // open: in6, in7, in8, in9, in10, in11, in12, in13, in14, in15, en

  // Notes on the sheet:
  //   B
endmodule

module Addl (
  input  in_1,
  input  in_2,
  input  in_3,
  output out_4,
  output out_5
);

  wire and_1_out, and_2_out, xor_1_out;

  and and_1 (and_1_out, in_1, in_2);
  xor xor_1 (xor_1_out, in_1, in_2);
  and and_2 (and_2_out, xor_1_out, in_3);
  xor xor_2 (out_4, xor_1_out, in_3);
  xor xor_3 (out_5, and_2_out, and_1_out);
endmodule

module add8 (
  input  Cin,
  input  [7:0] First_8_bits_input,
  input  [7:0] Second_8_bits_input,
  output [7:0] out_4,
  output Cout
);

  wire addl_1_out_5, addl_2_out_5, addl_3_out_5, addl_4_out_5, addl_5_out_5, addl_6_out_5, addl_7_out_5;

  Addl addl_1 (
    .in_1(First_8_bits_input[0]), .in_2(Second_8_bits_input[0]), .in_3(Cin), .out_4(out_4[0]),
    .out_5(addl_1_out_5));
  Addl addl_2 (
    .in_1(First_8_bits_input[1]), .in_2(Second_8_bits_input[1]), .in_3(addl_1_out_5), .out_4(out_4[1]),
    .out_5(addl_2_out_5));
  Addl addl_3 (
    .in_1(First_8_bits_input[2]), .in_2(Second_8_bits_input[2]), .in_3(addl_2_out_5), .out_4(out_4[2]),
    .out_5(addl_3_out_5));
  Addl addl_4 (
    .in_1(First_8_bits_input[3]), .in_2(Second_8_bits_input[3]), .in_3(addl_3_out_5), .out_4(out_4[3]),
    .out_5(addl_4_out_5));
  Addl addl_5 (
    .in_1(First_8_bits_input[4]), .in_2(Second_8_bits_input[4]), .in_3(addl_4_out_5), .out_4(out_4[4]),
    .out_5(addl_5_out_5));
  Addl addl_6 (
    .in_1(First_8_bits_input[5]), .in_2(Second_8_bits_input[5]), .in_3(addl_5_out_5), .out_4(out_4[5]),
    .out_5(addl_6_out_5));
  Addl addl_7 (
    .in_1(First_8_bits_input[6]), .in_2(Second_8_bits_input[6]), .in_3(addl_6_out_5), .out_4(out_4[6]),
    .out_5(addl_7_out_5));
  Addl addl_8 (
    .in_1(First_8_bits_input[7]), .in_2(Second_8_bits_input[7]), .in_3(addl_7_out_5), .out_4(out_4[7]),
    .out_5(Cout));
endmodule

module ZF (
  input  [7:0] in_1,
  output out_2
);

  wire or_1_out, or_2_out, or_3_out, or_4_out, or_5_out, or_6_out, or_7_out;

  or or_1 (or_1_out, in_1[0], in_1[1]);
  or or_2 (or_2_out, in_1[2], in_1[3]);
  or or_3 (or_3_out, in_1[4], in_1[5]);
  or or_4 (or_4_out, in_1[6], in_1[7]);
  or or_5 (or_5_out, or_1_out, or_2_out);
  or or_6 (or_6_out, or_3_out, or_4_out);
  or or_7 (or_7_out, or_5_out, or_6_out);
  not not_1 (out_2, or_7_out);
endmodule

module SF (
  input  [7:0] in_1,
  output SF
);

  wire and_1_out, and_2_out, and_3_out, and_4_out, and_5_out, and_6_out, and_7_out;

  and and_1 (and_1_out, in_1[0], in_1[1]);
  and and_2 (and_2_out, in_1[2], in_1[3]);
  and and_3 (and_3_out, in_1[4], in_1[5]);
  and and_4 (and_4_out, and_1_out, and_2_out);
  and and_5 (and_5_out, and_3_out, in_1[6]);
  and and_6 (and_6_out, and_4_out, and_5_out);
  and and_7 (and_7_out, and_6_out, in_1[7]);
  or or_1 (SF, and_7_out, in_1[7]);
endmodule

module Right_Shift (
  input  [7:0] in_1,
  input  Cin,
  output Cout,
  output [7:0] out_4
);


  assign Cout = in_1[0];
  assign out_4 = {Cin, in_1[7:1]};
endmodule

module ALU (
  input  [7:0] A,
  input  [7:0] B,
  input  Cin,
  input  [3:0] OP,
  output ZF,
  output SF,
  output OF,
  output Cout,
  output [7:0] F
);

  Main main_1 (.A(A), .B(B), .Cin(Cin), .ZF(ZF), .SF(SF), .OF(OF), .Cout(Cout), .Selector_PIn(OP), ._8_bits_output(F));
endmodule

module Left_Shift (
  input  Cin,
  input  [7:0] Input,
  output [7:0] out_3,
  output Cout
);


  assign Cout = Input[7];
  assign out_3 = {Input[6:0], Cin};
endmodule

module OF (
  input  [7:0] Output,
  input  [7:0] Input_A,
  input  [3:0] Selector,
  input  [7:0] Input_B,
  output OF
);

  wire and_1_out, not_2_out, or_1_out, xor_1_out, xor_2_out;
  wire [7:0] multiplexer_1_out, not_1_out;

  assign not_1_out = ~Input_A;  // NOT_Gate not_1, 8 bits wide
  Multiplexer #(.select(4), .width(8)) multiplexer_1 (
    .in0(Input_A), .in1(not_1_out), .out(multiplexer_1_out), .sel(Selector));  // open: in2, in3, in4, in5, in6, in7, in8, in9, in10, in11, in12, in13, in14, in15, en
  xor xor_1 (xor_1_out, multiplexer_1_out[7], Input_B[7]);
  not not_2 (not_2_out, xor_1_out);
  and and_1 (and_1_out, Input_B[7], multiplexer_1_out[7]);
  or or_1 (or_1_out, not_2_out, and_1_out);
  xor xor_2 (xor_2_out, Output[7], and_1_out);
  and and_2 (OF, xor_2_out, or_1_out);
endmodule
