// Logisim project y86.circ as structural Verilog: 5 circuits, main circuit main
module main (
  input  Reset
);

  wire and_1_out, Clock_out, nor_1_out, not_1_out;
  wire [1:0] imem_1_p2, Stat_q;
  wire [31:0] PC_q, PChold_q;

  and and_1 (and_1_out, Clock_out, nor_1_out);
  Clock Clock (.out(Clock_out));
  Register #(.width(32)) PC (.D(PChold_q), .Q(PC_q), .clk(and_1_out), .clr(Reset));  // open: en
  nor nor_1 (nor_1_out, Stat_q[1], Stat_q[0]);
  not not_1 (not_1_out, and_1_out);
  Register #(.width(2)) Stat (.D(imem_1_p2), .Q(Stat_q), .clk(not_1_out));  // open: en, clr
  // imem imem_1: pin names not known; wires that end beside it: PC_q, imem_1_p2
  Register #(.width(32)) PChold (.Q(PChold_q), .clk(not_1_out), .clr(Reset));  // open: D, en
endmodule

module Align (
  input  [7:0] B1,
  input  [7:0] B2,
  input  [7:0] B3,
  input  [7:0] B4,
  input  [7:0] B5,
  input  [7:0] B6,
  input  [7:0] B7,
  input  [7:0] B8,
  input  NeedRegs,
  input  [7:0] B9,
  output [3:0] rA,
  output [3:0] rB,
  output [31:0] valC_0,
  output [31:0] valC_1
);

  Multiplexer #(.width(32), .enable("false")) multiplexer_1 (
    .in0({B4, B3, B2, B1}), .in1({B5, B4, B3, B2}), .out(valC_0), .sel(NeedRegs));
  Multiplexer #(.width(32), .enable("false")) multiplexer_2 (
    .in0({B8, B7, B6, B5}), .in1({B9, B8, B7, B6}), .out(valC_1), .sel(NeedRegs));

  assign rA = B1[3:0];
  assign rB = B1[7:4];
endmodule

module Fetch (
  input  [7:0] in_1,
  input  [7:0] in_2,
  input  [7:0] in_3,
  input  [7:0] in_4,
  input  [7:0] in_5,
  input  [7:0] in_6,
  input  [7:0] in_7,
  input  [7:0] in_8,
  input  [7:0] in_9,
  input  [7:0] in_10,
  output [3:0] out_11,
  output [3:0] out_12
);

  wire needreg_1_needreg;

  needReg needreg_1 (.icode(in_1[3:0]), .needReg(needreg_1_needreg));
  Align align_1 (
    .B1(in_2), .B2(in_3), .B3(in_4), .B4(in_5), .B5(in_6), .B6(in_7), .B7(in_8), .B8(in_9), .B9(in_10),
    .NeedRegs(needreg_1_needreg));  // open: rA, rB, valC_0, valC_1

  assign out_11 = in_1[3:0];
  assign out_12 = in_1[7:4];
endmodule

module needReg (
  input  [3:0] icode,
  output needReg
);

  Multiplexer #(.select(4), .enable("false")) multiplexer_1 (
    .in0(1'b0), .in1(1'b0), .in2(1'b1), .in3(1'b1), .in4(1'b1), .in5(1'b1), .in6(1'b1), .in7(1'b0),
    .in8(1'b0), .in9(1'b0), .in10(1'b1), .in11(1'b1), .out(needReg), .sel(icode));  // open: in12, in13, in14, in15
endmodule

module needValC (
  input  [3:0] icode,
  output needsValC
);

  Multiplexer #(.select(4), .enable("false")) multiplexer_1 (
    .in0(1'b0), .in1(1'b0), .in2(1'b0), .in3(1'b0), .in4(1'b1), .in5(1'b1), .in6(1'b1), .in7(1'b0),
    .in8(1'b1), .in9(1'b1), .in10(1'b0), .in11(1'b0), .in12(1'b0), .out(needsValC), .sel(icode));  // open: in13, in14, in15
endmodule
